// Digital circuit Processador.dig as structural Verilog
module Processador (
  input  in_1
);

  SinalEXt sinalext_1 ();  // open: In, Out
  ULA ula_1 ();  // open: Alpha, Beta, fun, Gamma
  ROM rom_1 ();  // open: A, sel, D
  Registrador32bit registrador32bit_1 ();  // open: Enable, Clk, c, a_2, b_2, C_2, A, B
  Seven_Seg_Hex seven_seg_hex_1 ();  // open: d, dp
endmodule
